// Logisim project Adder_and_Halfadder.circ as structural Verilog: 1 circuit, main circuit main
module main (
  input  bit_1,
  input  bit_2,
  input  A_bit_1,
  input  B_bit_1,
  input  cary
);

  wire and_1_out, and_2_out, and_3_out, or_1_out, xor_1_out, xor_2_out, xor_3_out;

  LED led_1 (.in(bit_1));
  LED led_2 (.in(bit_2));
  LED led_3 (.in(A_bit_1));
  LED led_4 (.in(B_bit_1));
  xor xor_1 (xor_1_out, bit_1, bit_2);
  and and_1 (and_1_out, bit_1, bit_2);
  xor xor_2 (xor_2_out, A_bit_1, B_bit_1);
  and and_2 (and_2_out, A_bit_1, B_bit_1);
  LED led_5 (.in(xor_1_out));
  LED led_6 (.in(and_1_out));
  xor xor_3 (xor_3_out, xor_2_out, cary);
  and and_3 (and_3_out, xor_2_out, cary);
  or or_1 (or_1_out, and_2_out, and_3_out);
  LED led_7 (.in(xor_3_out));
  LED led_8 (.in(or_1_out));

  // Notes on the sheet:
  //   xor
  //   and
  //   xor
  //   and
  //   sum
  //   cary
  //   sub_sum
  //   xor
  //   and
  //   sum 1
  //   or
  //   cary
endmodule
