// Logisim project Board.circ as structural Verilog: 1 circuit, main circuit main
module main (
  input  A_bit_4,
  input  A_bit_3,
  input  A_bit_2,
  input  A_bit_1,
  input  B_bit_4,
  input  B_bit_3,
  input  B_bit_2,
  input  B_bit_1,
  input  cary
);

  wire and_1_out, and_2_out, and_3_out, and_4_out, and_5_out, and_6_out, and_7_out, and_8_out, or_1_out,
       or_2_out, or_3_out, or_4_out, xor_1_out, xor_2_out, xor_3_out, xor_4_out, xor_5_out, xor_6_out,
       xor_7_out, xor_8_out;

  LED led_1 (.in(A_bit_4));
  LED led_2 (.in(B_bit_4));
  LED led_3 (.in(B_bit_3));
  LED led_4 (.in(A_bit_3));
  LED led_5 (.in(A_bit_2));
  LED led_6 (.in(B_bit_2));
  xor xor_1 (xor_1_out, A_bit_4, B_bit_4);
  and and_1 (and_1_out, A_bit_4, B_bit_4);
  LED led_7 (.in(A_bit_1));
  LED led_8 (.in(B_bit_1));
  xor xor_2 (xor_2_out, A_bit_3, B_bit_3);
  and and_2 (and_2_out, A_bit_3, B_bit_3);
  xor xor_3 (xor_3_out, xor_1_out, or_2_out);
  and and_3 (and_3_out, xor_1_out, or_2_out);
  xor xor_4 (xor_4_out, A_bit_1, B_bit_1);
  and and_4 (and_4_out, A_bit_1, B_bit_1);
  xor xor_5 (xor_5_out, A_bit_2, B_bit_2);
  and and_5 (and_5_out, A_bit_2, B_bit_2);
  xor xor_6 (xor_6_out, xor_2_out, or_4_out);
  and and_6 (and_6_out, xor_2_out, or_4_out);
  or or_1 (or_1_out, and_1_out, and_3_out);
  xor xor_7 (xor_7_out, xor_4_out, cary);
  and and_7 (and_7_out, xor_4_out, cary);
  xor xor_8 (xor_8_out, xor_5_out, or_3_out);
  and and_8 (and_8_out, xor_5_out, or_3_out);
  or or_2 (or_2_out, and_2_out, and_6_out);
  or or_3 (or_3_out, and_4_out, and_7_out);
  or or_4 (or_4_out, and_5_out, and_8_out);
  LED led_9 (.in(or_1_out));
  LED led_10 (.in(xor_3_out));
  LED led_11 (.in(xor_6_out));
  LED led_12 (.in(xor_8_out));
  LED led_13 (.in(xor_7_out));

  // Notes on the sheet:
  //   A_bit_4
  //   B_bit_4
  //   cary
  //   A_bit_3
  //   B_bit_3
  //   cary
  //   xor
  //   and
  //   A_bit_2
  //   B_bit_2
  //   cary
  //   xor
  //   and
  //   sub_sum
  //   sub_sum
  //   sum 1
  //   xor
  //   and
  //   xor
  //   and
  //   xor
  //   and
  //   xor
  //   and
  //   cary 1_1
  //   cary 1_2
  //   sub_sum
  //   sub_sum
  //   sum 1
  //   cary 1_1
  //   cary 1_2
  //   cary
  //   or
  //   xor
  //   and
  //   xor
  //   and
  //   or
  //   sum 1
  //   sum 1
  //   cary 1_1
  //   cary 1_2
  //   cary
  //   or
  //   or
  //   cary
  //   cary
  //   cary
  //   bit_4
  //   bit_3
  //   bit_2
  //   bit_1
endmodule
